# Fritzing sketch microelectronics_intro (saved by Fritzing 1.0.1rc)
breadboards: 1

parts:
  A2 = photon2
  S2 = Pushbutton [package=THT]
  R3 = Resistor [tolerance=±5% power=0.25W resistance=220 package=THT]
  LED2 = LED - 5mm [color="Green (560nm)" current=0.030A package="5 mm [THT]"]

nets:
  N1: A2.Pin_2, S2.leg1
  N2: A2.Pin_4, A2.Pin_30, LED2.cathode
  N3: A2.Pin_19, S2.leg0
  N4: A2.Pin_20, R3.Pin_0
  N5: A2.Pin_28, A2.Pin_29
  N6: R3.Pin_1, LED2.anode

custom parts:
  photon2: The Photon 2 is a development module with a microcontroller and Wi-Fi networking.
